# Fritzing sketch ikea lights (saved by Fritzing 0.9.3b)
breadboards: 1

parts:
  U1 = PIC 16F688 [package=soic-14]
  R1 = Resistor [tolerance=±5% resistance=10k package=THT]
  R2 = Resistor [tolerance=±5% resistance=10k package=THT]
  R3 = Resistor [tolerance=±5% resistance=10k package=THT]
  R4 = Resistor [tolerance=±5% resistance=100 package=THT]
  R5 = Resistor [tolerance=±5% resistance=150 package=THT]
  R6 = Resistor [tolerance=±5% resistance=150 package=THT]
  R7 = Resistor [tolerance=±5% resistance=150 package=THT]
  S1 = Pushbutton [package="[THT]"]
  S2 = Pushbutton [package="[THT]"]
  S3 = Pushbutton [package="[THT]"]
  Q1 = Basic FET P-Channel [package="TO220 [THT]"]
  Q2 = Basic FET P-Channel [package="TO220 [THT]"]
  Q3 = Basic FET P-Channel [package="TO220 [THT]"]
  R8 = Trimmer Potentiometer [maximum_resistance=100kΩ package=THT]

nets:
  12V: U1.VDD, R1.Pin_0, R2.Pin_0, R3.Pin_0, R8.leg1
  N1: U1.RA4_OSC2, R1.Pin_1, S1.Pin_1, S1.Pin_2
  N2: U1.RA3_MCLR, R2.Pin_1, S2.Pin_1, S2.Pin_2
  N3: U1.RC5_RX, R3.Pin_1, S3.Pin_1, S3.Pin_2
  N4: U1.RC3_AN7, R4.Pin_1
  N5: U1.RA2_AN2, R7.Pin_0
  N6: U1.RA1_PGC, R6.Pin_0
  N7: U1.RA0_PGD, R5.Pin_0
  GND: U1.VSS, S1.Pin_3, S1.Pin_4, S2.Pin_3, S2.Pin_4, S3.Pin_3, S3.Pin_4, Q1.source, Q2.source, Q3.source, R8.leg2
  N8: R4.Pin_0, R8.wiper
  N9: R5.Pin_1, Q1.gate
  N10: R6.Pin_1, Q2.gate
  N11: R7.Pin_1, Q3.gate
