# Fritzing sketch light controls (saved by Fritzing 0.9.3b)
circuit board: 8.46667cm x 5.64444cm
stripboards: 1

parts:
  IC1 = IC, DIP package, 14 pins [chip_label=ATTiny84]
  J1 = female pin header, 6 pins [form="♀ (female)"]
  J2 = female pin header, 3 pins [form="♀ (female)"]
  J3 = female pin header, 3 pins [form="♀ (female)"]
  J4 = female pin header, 4 pins [form="♀ (female)"]

nets:
  N1: IC1.pin1, J1.pin2, J2.pin3, J3.pin3, J4.pin1
  N2: IC1.pin5, J1.pin5
  N3: IC1.pin6, J1.pin6
  N4: IC1.pin7, J4.pin2
  N5: IC1.pin8, J1.pin4
  N6: IC1.pin9, J4.pin3
  N7: IC1.pin11, J3.pin2
  N8: IC1.pin12, J2.pin2
  N9: IC1.pin13, J1.pin3
  N10: IC1.pin14, J1.pin1, J2.pin1, J3.pin1, J4.pin4
