# Fritzing sketch light controls (saved by Fritzing 0.9.3b)
stripboards: 1

parts:
  IC1 = IC, DIP package, 14 pins [chip_label=ATTiny84]
  J1 = female pin header, 6 pins [form="♀ (female)"]

nets:
  N1: IC1.pin1, J1.pin1
  N2: IC1.pin10, J1.pin6
  N3: IC1.pin11, J1.pin5
  N4: IC1.pin12, J1.pin4
  N5: IC1.pin13, J1.pin3
  N6: IC1.pin14, J1.pin2
